// Logisim project KT8.circ as structural Verilog: 3 circuits, main circuit main
module main (
);

  wire and_1_out, and_2_out, clock_1_out, comparator_1_eq, comparator_1_gt, cpu_1_reset_k_d, cpu_1_w_nr,
       nor_1_out, not_1_out, not_2_out, or_1_out, Reset_out, RKD_out;
  wire [3:0] cpu_1_address;
  wire [6:0] bit_extender_2_out, keyboard_1_data;
  wire [7:0] bit_extender_1_out, controlled_buffer_1_out, cpu_1_code_address, cpu_1_ram_out, rom_1_data;

  cpu cpu_1 (
    .Reset(Reset_out), .Instruction(rom_1_data), .RAM_in(controlled_buffer_1_out), .Clock(clock_1_out),
    .Code_address(cpu_1_code_address), .Address(cpu_1_address), .RAM_out(cpu_1_ram_out), .W_nR(cpu_1_w_nr),
    .Reset_K_D(cpu_1_reset_k_d));
  Button Reset (.out(Reset_out));
  Clock clock_1 (.out(clock_1_out));
  ROM rom_1 (.addr(cpu_1_code_address), .data(rom_1_data));  // open: sel
  Comparator #(.width(4), .mode("unsigned")) comparator_1 (
    .a(cpu_1_address), .b(4'b1110), .gt(comparator_1_gt), .eq(comparator_1_eq));  // open: lt
  nor nor_1 (nor_1_out, comparator_1_gt, comparator_1_eq);
  or or_1 (or_1_out, cpu_1_reset_k_d, RKD_out);
  Button RKD (.out(RKD_out));
  not not_1 (not_1_out, cpu_1_w_nr);
  Keyboard keyboard_1 (.clk(clock_1_out), .re(and_1_out), .clr(or_1_out), .data(keyboard_1_data));  // open: avail
  not not_2 (not_2_out, nor_1_out);
  and and_1 (and_1_out, not_2_out, ~cpu_1_address[0]);  // AND_Gate
  assign controlled_buffer_1_out = and_1_out ? bit_extender_1_out : 8'bz;  // Controlled_Buffer controlled_buffer_1
  RAM #(.addrWidth(4), .bus("separate")) ram_1 (
    .addr(cpu_1_address), .din(cpu_1_ram_out), .data(controlled_buffer_1_out), .str(cpu_1_w_nr),
    .sel(nor_1_out), .clk(clock_1_out), .ld(not_1_out));  // open: clr
  assign bit_extender_1_out = {{1{1'b0}}, keyboard_1_data};  // Bit_Extender bit_extender_1
  Bit_Extender #(.out_width(7)) bit_extender_2 (.in(cpu_1_ram_out), .out(bit_extender_2_out));
  TTY tty_1 (.data(bit_extender_2_out), .clk(clock_1_out), .we(and_2_out), .clr(or_1_out));
  and and_2 (and_2_out, cpu_1_address[0], not_2_out);
endmodule

module cpu (
  input  Reset,
  input  [7:0] Instruction,
  input  [7:0] RAM_in,
  input  Clock,
  output [7:0] Code_address,
  output [3:0] Address,
  output [7:0] RAM_out,
  output W_nR,
  output Reset_K_D
);

  wire and_1_out, decoder_1_out0, decoder_1_out1, decoder_1_out3, decoder_1_out4, decoder_1_out7,
       decoder_1_out8, decoder_2_out0, decoder_2_out1, or_1_out, or_2_out;
  wire [7:0] alu_1_r, bit_extender_1_out, multiplexer_1_out, register_1_q, register_2_q;

  and and_1 (and_1_out, Clock, ~decoder_2_out1);  // AND_Gate
  Decoder #(.select(4), .disabled(0), .enable("false")) decoder_1 (
    .out0(decoder_1_out0), .out1(decoder_1_out1), .out2(W_nR), .out3(decoder_1_out3), .out4(decoder_1_out4),
    .out7(decoder_1_out7), .out8(decoder_1_out8), .out9(Reset_K_D), .sel(Instruction[7:4]));  // open: out5, out6, out10, out11, out12, out13, out14, out15
  or or_1 (or_1_out, decoder_1_out7, decoder_1_out8, decoder_1_out4);
  Decoder #(.select(4), .disabled(0)) decoder_2 (
    .out0(decoder_2_out0), .out1(decoder_2_out1), .sel(Instruction[3:0]), .en(or_1_out));  // open: out2, out3, out4, out5, out6, out7, out8, out9, out10, out11, out12, out13, out14, out15
  assign bit_extender_1_out = {{4{1'b0}}, Instruction[3:0]};  // Bit_Extender bit_extender_1
  Register register_1 (.D(RAM_in), .en(decoder_1_out0), .Q(register_1_q), .clk(and_1_out));  // open: clr
  Multiplexer #(.width(8), .disabled(0), .enable("false")) multiplexer_1 (
    .in0(RAM_in), .in1(bit_extender_1_out), .out(multiplexer_1_out), .sel(decoder_1_out3));
  Register register_2 (.D(multiplexer_1_out), .en(decoder_1_out1), .Q(register_2_q), .clk(and_1_out));  // open: clr
  Register register_3 (.D(alu_1_r), .en(decoder_1_out4), .Q(RAM_out), .clk(and_1_out));  // open: clr
  alu alu_1 (.A(register_1_q), .B(register_2_q), .Op(Instruction[3:0]), .R(alu_1_r));
  Counter counter_1 (.count(1'b1), .Q(Code_address), .clk(and_1_out), .clr(or_2_out));  // open: load, D, carry
  or or_2 (or_2_out, decoder_2_out0, Reset);

  assign Address = Instruction[3:0];

  // Notes on the sheet:
  //   Clock: pull=down
endmodule

module alu (
  input  [7:0] A,
  input  [7:0] B,
  input  [3:0] Op,
  output [7:0] R
);

  wire [7:0] adder_1_out, and_1_out, not_1_out, not_2_out, or_1_out, shifter_1_out, shifter_2_out,
       subtractor_1_out, xor_1_out;

  Adder adder_1 (.a(A), .b(B), .out(adder_1_out));  // open: cin, cout
  Subtractor subtractor_1 (.a(A), .b(B), .out(subtractor_1_out));  // open: bin, bout
  assign and_1_out = A & B;  // AND_Gate and_1, 8 bits wide
  assign or_1_out = A | B;  // OR_Gate or_1, 8 bits wide
  assign xor_1_out = A ^ B;  // XOR_Gate xor_1, 8 bits wide
  assign not_1_out = ~A;  // NOT_Gate not_1, 8 bits wide
  assign not_2_out = ~B;  // NOT_Gate not_2, 8 bits wide
  Shifter shifter_1 (.in(A), .\dist (3'b001), .out(shifter_1_out));
  Shifter #(.shift("lr")) shifter_2 (.in(A), .\dist (3'b001), .out(shifter_2_out));
  Adder adder_2 (.a(A), .b(8'h1));  // open: out, cin, cout
  Subtractor subtractor_2 (.a(A), .b(8'h1));  // open: out, bin, bout
  Multiplexer #(.select(4), .width(8), .disabled(0), .enable("false")) multiplexer_1 (
    .in0(adder_1_out), .in1(subtractor_1_out), .in2(and_1_out), .in3(or_1_out), .in4(xor_1_out),
    .in5(not_1_out), .in6(not_2_out), .in7(A), .in8(B), .in9(shifter_1_out), .in10(shifter_2_out),
    .in11({8{1'b0}}), .out(R), .sel(Op));  // open: in12, in13, in14, in15
endmodule
